# Fritzing sketch hotspot-1d-shield (saved by Fritzing 0.9.3b)
circuit board: 6.88566cm x 5.36311cm
breadboards: 1

parts:
  TMP00x = TMP006 Thermopile Sensor
  MicroSD = MicroSD Card Module
  R1 = Resistor [tolerance=±5% resistance=330 package=THT]
  R2 = Resistor [tolerance=±5% resistance=330 package=THT]
  LED1 = LED - 5mm [color="Red (633nm)" package="5 mm [THT]"]
  LED2 = LED - 5mm [color="Green (555nm)" package="5 mm [THT]"]
  R3 = Resistor [tolerance=±5% resistance=10k package=THT]
  R4 = Resistor [tolerance=±5% resistance=10k package=THT]
  R5 = Resistor [tolerance=±5% resistance=10k package=THT]
  PCB = Arduino Shield PCB  # not connected
  RESET = Pushbutton [package="[THT]"]
  Arduino = Arduino Uno (Rev3)
  TMP36 = TMP36 [package=to-92-kit]
  TRS1 = Audio Jack (TRS) 3.5mm [package="4Ucon 08780 [THT]"]

nets:
  VCC: TMP00x.VCC, MicroSD.VCC, R5.Pin_1, Arduino.5V, TMP36.VCC, TRS1.Sleeve
  GND: TMP00x.GND, MicroSD.GND, LED1.anode, LED2.anode, R3.Pin_1, R4.Pin_1, RESET.Pin_3, RESET.Pin_4, Arduino.GND, TMP36.GND
  N1: TMP00x.SDA, Arduino.A4/SDA
  N2: TMP00x.SCL, Arduino.A5/SCL
  N3: MicroSD.MISO, Arduino.D12/MISO
  N4: MicroSD.MOSI, Arduino.D11_PWM/MOSI
  N5: MicroSD.SCK, Arduino.D13/SCK
  N6: MicroSD.CS, Arduino.D4
  N7: R1.Pin_0, LED1.cathode
  N8: R1.Pin_1, Arduino.D9_PWM
  N9: R2.Pin_0, LED2.cathode
  N10: R2.Pin_1, Arduino.D8
  N11: R3.Pin_0, Arduino.D6_PWM, TRS1.Tip
  N12: R4.Pin_0, Arduino.D7, TRS1.Ring
  N13: R5.Pin_0, RESET.Pin_1, RESET.Pin_2, Arduino.RESET
  N14: Arduino.A3, TMP36.VOUT

notes:
  github.com/NehenemiLabs/hotspot-1d
  Hotspot 1D
  0.5b

custom parts:
  TMP006 Thermopile Sensor: Unlike all the other temperature sensors we have, this breakout has a really cool IR sensor from TI that can measure the temperature of an object without touching it! Simply point the sensor towards what you want to measure and it will detect the temperature by absorbing IR waves emitted. The embedded thermopile sensor generates a very very small voltage depending on how much IR there is, and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
  Arduino Shield PCB: Plain PCB Shaped to fit an Arduino "Shield"
